# Fritzing sketch automatica (saved by Fritzing 0.9.3b)

parts:
  Part1 = Arduino Yun
  PIR1 = PIR sensor
  Grove1 = Grove Light Sensor
  KY-1 = Keyes Relay [package=THT]

nets:
  N1: Part1.A0, Grove1.SIG
  GND: Part1.GND, PIR1.GND, Grove1.GND, KY-1.ground
  N2: Part1.D3/SCL, Part1.D3_PWM, KY-1.signal
  N3: Part1.D2, PIR1.SIG
  5V: Part1.5V, PIR1.VDD, Grove1.VCC, KY-1.power

custom parts:
  Keyes Relay: The Keyes 5V relay module is suitable for SCM development, home appliance control. It uses a 5V~12V TIL control signal which can control DC / AC signal.
